// Logisim project tp.circ as structural Verilog: 10 circuits, main circuit principal
// CONTADOR
module contador (
  input  \BOTÃO ,
  input  CLEAR,
  input  ENABLE,
  output [8:0] out_4
);

  wire j_k_ff_1_qn, j_k_ff_2_qn, j_k_ff_3_qn, j_k_ff_4_qn, j_k_ff_5_qn, j_k_ff_6_qn, j_k_ff_7_qn, j_k_ff_8_qn;

  J_K_Flip_Flop j_k_ff_1 (
    .J(1'b1), .clk(\BOTÃO ), .K(1'b1), .Q(out_4[0]), .Qn(j_k_ff_1_qn), .en(ENABLE), .reset(CLEAR));  // open: preset
  J_K_Flip_Flop j_k_ff_2 (
    .J(1'b1), .clk(j_k_ff_1_qn), .K(1'b1), .Q(out_4[1]), .Qn(j_k_ff_2_qn), .en(ENABLE), .reset(CLEAR));  // open: preset
  J_K_Flip_Flop j_k_ff_3 (
    .J(1'b1), .clk(j_k_ff_2_qn), .K(1'b1), .Q(out_4[2]), .Qn(j_k_ff_3_qn), .en(ENABLE), .reset(CLEAR));  // open: preset
  J_K_Flip_Flop j_k_ff_4 (
    .J(1'b1), .clk(j_k_ff_3_qn), .K(1'b1), .Q(out_4[3]), .Qn(j_k_ff_4_qn), .en(ENABLE), .reset(CLEAR));  // open: preset
  J_K_Flip_Flop j_k_ff_5 (
    .J(1'b1), .clk(j_k_ff_4_qn), .K(1'b1), .Q(out_4[4]), .Qn(j_k_ff_5_qn), .en(ENABLE), .reset(CLEAR));  // open: preset
  J_K_Flip_Flop j_k_ff_6 (
    .J(1'b1), .clk(j_k_ff_5_qn), .K(1'b1), .Q(out_4[5]), .Qn(j_k_ff_6_qn), .en(ENABLE), .reset(CLEAR));  // open: preset
  J_K_Flip_Flop j_k_ff_7 (
    .J(1'b1), .clk(j_k_ff_6_qn), .K(1'b1), .Q(out_4[6]), .Qn(j_k_ff_7_qn), .en(ENABLE), .reset(CLEAR));  // open: preset
  J_K_Flip_Flop j_k_ff_8 (
    .J(1'b1), .clk(j_k_ff_7_qn), .K(1'b1), .Q(out_4[7]), .Qn(j_k_ff_8_qn), .en(ENABLE), .reset(CLEAR));  // open: preset
  J_K_Flip_Flop j_k_ff_9 (
    .J(1'b1), .clk(j_k_ff_8_qn), .K(1'b1), .Q(out_4[8]), .en(ENABLE), .reset(CLEAR));  // open: Qn, preset
endmodule

module principal (
  input  ENABLE,
  input  EDISPLAY
);

  wire _0_out, _1_out, ADM, and_1_out, and_2_out, BOM_out, ENTER_out, OTIMO_out, PESSIMO_out, REGULAR_out,
       RESETA_CONTAGEM_out, RUIM_out;
  wire [3:0] separador_enable_1_out_3, separador_enable_1_out_4, separador_enable_1_out_5,
       separador_enable_2_out_3, separador_enable_2_out_4, separador_enable_2_out_5,
       separador_enable_3_out_3, separador_enable_3_out_4, separador_enable_3_out_5,
       separador_enable_4_out_3, separador_enable_4_out_4, separador_enable_4_out_5,
       separador_enable_5_out_3, separador_enable_5_out_4, separador_enable_5_out_5;
  wire [5:0] demux_emote_1_out_3, demux_emote_1_out_4, demux_emote_1_out_5, demux_emote_1_out_6,
       demux_emote_1_out_7, demux_emote_2_out_3, demux_emote_2_out_4, demux_emote_2_out_5,
       demux_emote_2_out_6, demux_emote_2_out_7, demux_emote_3_out_3, demux_emote_3_out_4,
       demux_emote_3_out_5, demux_emote_3_out_6, demux_emote_3_out_7, demux_emote_4_out_3,
       demux_emote_4_out_4, demux_emote_4_out_5, demux_emote_4_out_6, demux_emote_4_out_7,
       demux_emote_5_out_3, demux_emote_5_out_4, demux_emote_5_out_5, demux_emote_5_out_6,
       demux_emote_5_out_7;
  wire [7:0] input_senha_senha;
  wire [8:0] contador_1_out_4, contador_2_out_4, contador_3_out_4, contador_4_out_4, contador_5_out_4;

  contador contador_1 (.\BOTÃO (OTIMO_out), .CLEAR(and_1_out), .ENABLE(ENABLE), .out_4(contador_1_out_4));
  Button OTIMO (.out(OTIMO_out));
  contador contador_2 (.\BOTÃO (BOM_out), .CLEAR(and_1_out), .ENABLE(ENABLE), .out_4(contador_2_out_4));
  Button BOM (.out(BOM_out));
  contador contador_3 (.\BOTÃO (REGULAR_out), .CLEAR(and_1_out), .ENABLE(ENABLE), .out_4(contador_3_out_4));
  Button REGULAR (.out(REGULAR_out));
  contador contador_4 (.\BOTÃO (RUIM_out), .CLEAR(and_1_out), .ENABLE(ENABLE), .out_4(contador_4_out_4));
  Button RUIM (.out(RUIM_out));
  contador contador_5 (.\BOTÃO (PESSIMO_out), .CLEAR(and_1_out), .ENABLE(ENABLE), .out_4(contador_5_out_4));
  Button PESSIMO (.out(PESSIMO_out));
  and and_1 (and_1_out, RESETA_CONTAGEM_out, ADM);
  Button RESETA_CONTAGEM (.out(RESETA_CONTAGEM_out));
  Button ENTER (.out(ENTER_out));
  Button _1 (.out(_1_out));
  Button _0 (.out(_0_out));
  separador_enable separador_enable_1 (
    .in_1(contador_1_out_4), .ENABLE(and_2_out), .out_3(separador_enable_1_out_3),
    .out_4(separador_enable_1_out_4), .out_5(separador_enable_1_out_5));
  separador_enable separador_enable_2 (
    .in_1(contador_2_out_4), .ENABLE(and_2_out), .out_3(separador_enable_2_out_3),
    .out_4(separador_enable_2_out_4), .out_5(separador_enable_2_out_5));
  separador_enable separador_enable_3 (
    .in_1(contador_3_out_4), .ENABLE(and_2_out), .out_3(separador_enable_3_out_3),
    .out_4(separador_enable_3_out_4), .out_5(separador_enable_3_out_5));
  separador_enable separador_enable_4 (
    .in_1(contador_4_out_4), .ENABLE(and_2_out), .out_3(separador_enable_4_out_3),
    .out_4(separador_enable_4_out_4), .out_5(separador_enable_4_out_5));
  separador_enable separador_enable_5 (
    .in_1(contador_5_out_4), .ENABLE(and_2_out), .out_3(separador_enable_5_out_3),
    .out_4(separador_enable_5_out_4), .out_5(separador_enable_5_out_5));
  and and_2 (and_2_out, EDISPLAY, ENABLE, ADM);
  inputsenha input_senha (._1(_1_out), ._0(_0_out), .SENHA(input_senha_senha));
  LED led_1 (.in(ADM));
  senha check (.ENTER(ENTER_out), .SENHA(input_senha_senha), .ADM(ADM));
  Hex_Digit_Display hex_digit_display_1 (.value(separador_enable_1_out_3));  // open: dp
  Hex_Digit_Display hex_digit_display_2 (.value(separador_enable_1_out_4));  // open: dp
  Hex_Digit_Display hex_digit_display_3 (.value(separador_enable_2_out_3));  // open: dp
  Hex_Digit_Display hex_digit_display_4 (.value(separador_enable_2_out_4));  // open: dp
  Hex_Digit_Display hex_digit_display_5 (.value(separador_enable_3_out_4));  // open: dp
  Hex_Digit_Display hex_digit_display_6 (.value(separador_enable_3_out_3));  // open: dp
  Hex_Digit_Display hex_digit_display_7 (.value(separador_enable_4_out_4));  // open: dp
  Hex_Digit_Display hex_digit_display_8 (.value(separador_enable_4_out_3));  // open: dp
  Hex_Digit_Display hex_digit_display_9 (.value(separador_enable_5_out_3));  // open: dp
  Hex_Digit_Display hex_digit_display_10 (.value(separador_enable_5_out_4));  // open: dp
  Hex_Digit_Display hex_digit_display_11 (.value(separador_enable_1_out_5));  // open: dp
  Hex_Digit_Display hex_digit_display_12 (.value(separador_enable_2_out_5));  // open: dp
  Hex_Digit_Display hex_digit_display_13 (.value(separador_enable_3_out_5));  // open: dp
  Hex_Digit_Display hex_digit_display_14 (.value(separador_enable_4_out_5));  // open: dp
  Hex_Digit_Display hex_digit_display_15 (.value(separador_enable_5_out_5));  // open: dp
  DotMatrix #(.matrixcols(7), .matrixrows(6)) dotmatrix_1 (
    .col0({6{1'b0}}), .col1(demux_emote_1_out_3), .col2(demux_emote_1_out_4), .col3(demux_emote_1_out_5),
    .col4(demux_emote_1_out_6), .col5(demux_emote_1_out_7), .col6({6{1'b0}}));
  DotMatrix #(.matrixcols(7), .matrixrows(6)) dotmatrix_2 (
    .col0({6{1'b0}}), .col1(demux_emote_2_out_3), .col2(demux_emote_2_out_4), .col3(demux_emote_2_out_5),
    .col4(demux_emote_2_out_6), .col5(demux_emote_2_out_7), .col6({6{1'b0}}));
  DotMatrix #(.matrixcols(7), .matrixrows(6)) dotmatrix_3 (
    .col0({6{1'b0}}), .col1(demux_emote_3_out_3), .col2(demux_emote_3_out_4), .col3(demux_emote_3_out_5),
    .col4(demux_emote_3_out_6), .col5(demux_emote_3_out_7), .col6({6{1'b0}}));
  DotMatrix #(.matrixcols(7), .matrixrows(6)) dotmatrix_4 (
    .col0({6{1'b0}}), .col1(demux_emote_4_out_3), .col2(demux_emote_4_out_4), .col3(demux_emote_4_out_5),
    .col4(demux_emote_4_out_6), .col5(demux_emote_4_out_7), .col6({6{1'b0}}));
  DotMatrix #(.matrixcols(7), .matrixrows(6)) dotmatrix_5 (
    .col0({6{1'b0}}), .col1(demux_emote_5_out_3), .col2(demux_emote_5_out_4), .col3(demux_emote_5_out_5),
    .col4(demux_emote_5_out_6), .col5(demux_emote_5_out_7), .col6({6{1'b0}}));
  demux_emote demux_emote_1 (
    .in_1(ENABLE), .in_2(3'b000), .out_3(demux_emote_1_out_3), .out_4(demux_emote_1_out_4),
    .out_5(demux_emote_1_out_5), .out_6(demux_emote_1_out_6), .out_7(demux_emote_1_out_7));
  demux_emote demux_emote_2 (
    .in_1(ENABLE), .in_2(3'b001), .out_3(demux_emote_2_out_3), .out_4(demux_emote_2_out_4),
    .out_5(demux_emote_2_out_5), .out_6(demux_emote_2_out_6), .out_7(demux_emote_2_out_7));
  demux_emote demux_emote_3 (
    .in_1(ENABLE), .in_2(3'b010), .out_3(demux_emote_3_out_3), .out_4(demux_emote_3_out_4),
    .out_5(demux_emote_3_out_5), .out_6(demux_emote_3_out_6), .out_7(demux_emote_3_out_7));
  demux_emote demux_emote_4 (
    .in_1(ENABLE), .in_2(3'b011), .out_3(demux_emote_4_out_3), .out_4(demux_emote_4_out_4),
    .out_5(demux_emote_4_out_5), .out_6(demux_emote_4_out_6), .out_7(demux_emote_4_out_7));
  demux_emote demux_emote_5 (
    .in_1(ENABLE), .in_2(3'b100), .out_3(demux_emote_5_out_3), .out_4(demux_emote_5_out_4),
    .out_5(demux_emote_5_out_5), .out_6(demux_emote_5_out_6), .out_7(demux_emote_5_out_7));
endmodule

// DECOD
module decodificador (
  input  [3:0] in_1,
  output out_2,
  output out_3,
  output out_4,
  output out_5,
  output out_6,
  output out_7,
  output out_8,
  output out_9
);

  wire _0, _1, _2, _3, _4, _5, _6, _7, _8, _9;

  Decoder #(.select(4), .disabled(0), .enable("false")) decoder_1 (
    .out0(_0), .out1(_1), .out2(_2), .out3(_3), .out4(_4), .out5(_5), .out6(_6), .out7(_7), .out8(_8),
    .out9(_9), .sel(in_1));  // open: out10, out11, out12, out13, out14, out15
  or or_1 (out_2, _2, _3, _4, _5, _6, _8, _9);
  or or_2 (out_3, _0, _4, _5, _6, _8, _9);
  or or_3 (out_4, _0, _2, _3, _5, _6, _7, _8, _9);
  or or_4 (out_5, _0, _1, _2, _3, _4, _7, _8, _9);
  or or_5 (out_6, _0, _2, _6, _8);
  or or_6 (out_7, _0, _2, _3, _5, _6, _8, _9);
  or or_7 (out_8, _0, _1, _3, _4, _5, _6, _7, _8, _9);

  assign out_9 = 1'b0;
endmodule

// SEPARADOR
module separadordecimal (
  input  in_1,
  input  in_2,
  input  in_3,
  input  in_4,
  input  in_5,
  input  in_6,
  input  in_7,
  input  in_8,
  input  in_9,
  output out_10,
  output out_11,
  output out_12,
  output out_13,
  output out_14,
  output out_15,
  output out_16,
  output out_17,
  output out_18,
  output out_19,
  output out_20,
  output out_21
);

  wire [8:0] divider_1_rem;
  wire [8:4] divider_1_out, divider_2_out, divider_2_rem;

  Divider #(.width(9)) divider_1 (
    .a({in_9, in_8, in_7, in_6, in_5, in_4, in_3, in_2, in_1}), .b(9'h64),
    .out({divider_1_out, out_10, out_11, out_12, out_13}), .rem(divider_1_rem));  // open: upper
  Divider #(.width(9)) divider_2 (
    .a(divider_1_rem), .b(9'ha), .out({divider_2_out, out_17, out_16, out_15, out_14}),
    .rem({divider_2_rem, out_18, out_19, out_20, out_21}));  // open: upper
endmodule

// SEPARADOR
module separador_enable (
  input  [8:0] in_1,
  input  ENABLE,
  output [3:0] out_3,
  output [3:0] out_4,
  output [3:0] out_5
);

  wire [8:0] liga_desliga_out_3;

  zeradistri liga_desliga (.in_1(in_1), .ENABLE(ENABLE), .out_3(liga_desliga_out_3));
  separadordecimal separadordecimal_1 (
    .in_1(liga_desliga_out_3[0]), .in_2(liga_desliga_out_3[1]), .in_3(liga_desliga_out_3[2]),
    .in_4(liga_desliga_out_3[3]), .in_5(liga_desliga_out_3[4]), .in_6(liga_desliga_out_3[5]),
    .in_7(liga_desliga_out_3[6]), .in_8(liga_desliga_out_3[7]), .in_9(liga_desliga_out_3[8]),
    .out_10(out_3[3]), .out_11(out_3[2]), .out_12(out_3[1]), .out_13(out_3[0]), .out_18(out_5[3]),
    .out_19(out_5[2]), .out_20(out_5[1]), .out_21(out_5[0]), .out_14(out_4[0]), .out_15(out_4[1]),
    .out_16(out_4[2]), .out_17(out_4[3]));
endmodule

module zeradistri (
  input  [8:0] in_1,
  input  ENABLE,
  output [8:0] out_3
);

  and and_1 (out_3[0], in_1[0], ENABLE);
  and and_2 (out_3[1], in_1[1], ENABLE);
  and and_3 (out_3[2], in_1[2], ENABLE);
  and and_4 (out_3[3], in_1[3], ENABLE);
  and and_5 (out_3[4], in_1[4], ENABLE);
  and and_6 (out_3[5], in_1[5], ENABLE);
  and and_7 (out_3[6], in_1[6], ENABLE);
  and and_8 (out_3[7], in_1[7], ENABLE);
  and and_9 (out_3[8], in_1[8], ENABLE);
endmodule

module demux_emote (
  input  in_1,
  input  [2:0] in_2,
  output [5:0] out_3,
  output [5:0] out_4,
  output [5:0] out_5,
  output [5:0] out_6,
  output [5:0] out_7
);

  wire demultiplexer_1_out0, demultiplexer_1_out1, demultiplexer_1_out2, demultiplexer_1_out3,
       demultiplexer_1_out4;

  Demultiplexer #(.select(3), .enable("false")) demultiplexer_1 (
    .out0(demultiplexer_1_out0), .out1(demultiplexer_1_out1), .out2(demultiplexer_1_out2),
    .out3(demultiplexer_1_out3), .out4(demultiplexer_1_out4), .in(in_1), .sel(in_2));  // open: out5, out6, out7
  or or_1 (out_3[1], demultiplexer_1_out3, demultiplexer_1_out4);
  or or_2 (out_3[2], demultiplexer_1_out0, demultiplexer_1_out1);
  or or_3 (out_4[4], demultiplexer_1_out0, demultiplexer_1_out1, demultiplexer_1_out2, demultiplexer_1_out3, demultiplexer_1_out4);
  or or_4 (out_4[2], demultiplexer_1_out0, demultiplexer_1_out3, demultiplexer_1_out4);
  or or_5 (out_4[1], demultiplexer_1_out0, demultiplexer_1_out1, demultiplexer_1_out2);
  or or_6 (out_5[2], demultiplexer_1_out0, demultiplexer_1_out3);
  or or_7 (out_5[1], demultiplexer_1_out0, demultiplexer_1_out1, demultiplexer_1_out2, demultiplexer_1_out4);
  or or_8 (out_6[4], demultiplexer_1_out0, demultiplexer_1_out1, demultiplexer_1_out2, demultiplexer_1_out3, demultiplexer_1_out4);
  or or_9 (out_6[2], demultiplexer_1_out0, demultiplexer_1_out3, demultiplexer_1_out4);
  or or_10 (out_6[1], demultiplexer_1_out0, demultiplexer_1_out1, demultiplexer_1_out2);
  or or_11 (out_7[1], demultiplexer_1_out3, demultiplexer_1_out4);
  or or_12 (out_7[2], demultiplexer_1_out0, demultiplexer_1_out1);

  assign {out_3[5:3], out_3[0]} = 4'b0000;
  assign {out_4[5], out_4[3], out_4[0]} = 3'b000;
  assign {out_5[5:3], out_5[0]} = 4'b0000;
  assign {out_6[5], out_6[3], out_6[0]} = 3'b000;
  assign {out_7[5:3], out_7[0]} = 4'b0000;
endmodule

module inputsenha (
  input  _1,
  input  _0,
  output [7:0] SENHA
);

  wire or_1_out;

  D_Flip_Flop d_ff_1 (.clk(or_1_out), .Q(SENHA[7]), .preset(_1), .reset(_0));  // open: D, Qn, en
  or or_1 (or_1_out, _1, _0);
  D_Flip_Flop d_ff_2 (.clk(or_1_out), .D(SENHA[7]), .Q(SENHA[6]));  // open: Qn, preset, en, reset
  D_Flip_Flop d_ff_3 (.clk(or_1_out), .D(SENHA[6]), .Q(SENHA[5]));  // open: Qn, preset, en, reset
  D_Flip_Flop d_ff_4 (.clk(or_1_out), .D(SENHA[5]), .Q(SENHA[4]));  // open: Qn, preset, en, reset
  D_Flip_Flop d_ff_5 (.clk(or_1_out), .D(SENHA[4]), .Q(SENHA[3]));  // open: Qn, preset, en, reset
  D_Flip_Flop d_ff_6 (.clk(or_1_out), .D(SENHA[3]), .Q(SENHA[2]));  // open: Qn, preset, en, reset
  D_Flip_Flop d_ff_7 (.clk(or_1_out), .D(SENHA[2]), .Q(SENHA[1]));  // open: Qn, preset, en, reset
  D_Flip_Flop d_ff_8 (.clk(or_1_out), .D(SENHA[1]), .Q(SENHA[0]));  // open: Qn, preset, en, reset
endmodule

module senha (
  input  ENTER,
  input  [7:0] SENHA,
  output ADM
);

  wire comparator_1_eq, not_1_out;
  wire [7:0] rom_1_data;

  ROM rom_1 (.addr({8{1'b0}}), .data(rom_1_data));  // open: sel
  Comparator #(.mode("unsigned")) comparator_1 (.a(SENHA), .b(rom_1_data), .eq(comparator_1_eq));  // open: gt, lt
  J_K_Flip_Flop j_k_ff_1 (
    .J(comparator_1_eq), .clk(ENTER), .K(not_1_out), .Q(ADM), .en(1'b1));  // open: Qn, preset, reset
  not not_1 (not_1_out, comparator_1_eq);

  // Notes on the sheet:
  //   contents of rom_1 (hex, n*v repeats v):
  //   70
endmodule

module salvar (
  input  in_1
);

  wire [7:0] counter_1_q;
  wire [8:0] rom_1_data;

  Counter #(.ongoal("continue")) counter_1 (.load(1'b0), .Q(counter_1_q), .clk(in_1));  // open: D, count, carry, clr
  ROM #(.dataWidth(9)) rom_1 (.addr(counter_1_q), .data(rom_1_data));  // open: sel
endmodule
